# Fritzing sketch Monitor connection (saved by Fritzing 0.9.6b)

parts:
  Componente2 = OLED Monochrome 128x64 0.96 inch [part_number=326]
  J1 = STM32 Nucleo boards

nets:
  N1: Componente2.MOSI_SDA, J1.A4/SDA
  N2: Componente2.SCLK_SCK, J1.A5/SCL
  VIN: Componente2.VIN, J1.5V
  GND: Componente2.GND, J1.GND

custom parts:
  OLED Monochrome 128x64 0.96 inch: These displays are small, only about 1" diameter, but very readable due to the high contrast of an OLED display. This display is made of 128x64 individual white OLED pixels, each one is turned on or off by the controller chip. Because the display makes its own light, no backlight is required. This reduces the power required to run the OLED and is why the display has such high contrast; we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
