# Fritzing sketch dock_device_connection (saved by Fritzing 0.9.6b)

parts:
  J1 = STM32 Nucleo boards
  HC-SR04_Sensor_1 = HC-SR04 Ultrasonic Distance Sensor
  LED1 = LED - 5mm [color="Red (633nm)" package="5 mm [THT]"]
  R1 = Resistor [tolerance=±5% resistance=220 package=THT]

nets:
  N1: J1.GND#1157, R1.Pin_0
  N2: J1.D2, HC-SR04_Sensor_1.ECHO
  N3: J1.D3_PWM, HC-SR04_Sensor_1.TRIG
  N4: J1.D4, LED1.anode
  5V: J1.5V, HC-SR04_Sensor_1.VCC
  N5: J1.GND#1188, HC-SR04_Sensor_1.GND
